# Fritzing sketch biribiri (saved by Fritzing 0.9.4)
breadboards: 1

parts:
  R1 = Resistor [tolerance=±5% resistance=3.3k package=THT]
  R2 = Resistor [tolerance=±5% resistance=22k package=THT]
  R3 = Resistor [tolerance=±5% resistance=3.3k package=THT]
  R4 = Resistor [tolerance=±5% resistance=10k package=THT]
  D1 = Rectifier Diode [part_number=1N4001 package="300 mil [THT]"]
  D2 = Rectifier Diode [part_number=1N4001 package="300 mil [THT]"]
  パーツ1 = Arduino Uno (Rev3)
  R5 = Resistor [tolerance=±5% resistance=10k package=THT]
  Q1 = NPN-Transistor [package="TO92 [THT]"]

nets:
  N1: R1.Pin_0, R5.Pin_1
  2: R1.Pin_1
  N2: R2.Pin_0, R4.Pin_0, パーツ1.5V, R5.Pin_0
  N3: R2.Pin_1, D2.cathode, Q1.C
  N4: R3.Pin_0, D1.anode
  1: R3.Pin_1
  N5: R4.Pin_1, D2.anode, パーツ1.D2
  N6: D1.cathode, Q1.B
  GND: パーツ1.GND, Q1.E
